// Logisim project MIPS_rodrigo.circ as structural Verilog: 9 circuits, main circuit main
module main (
  input  Manual,
  input  CLK,
  input  in_3,
  input  Restart,
  input  in_5,
  input  in_6,
  input  Clear,
  input  in_8,
  input  in_9,
  input  in_10,
  input  in_11,
  input  in_12,
  input  in_13,
  input  in_14,
  input  in_15
);

  wire alu_16bits_3_zero, and_1_out, Automatico_out, Clear_t, CLK_t, controlled_buffer_1_out, d_ff_1_q,
       not_1_out, not_2_out, not_3_out, not_4_out;
  wire [2:0] multiplexer_2_out;
  wire [4:0] program_cointer_1_saida;
  wire [6:0] memoriaDeInstrucoes_data;
  wire [15:0] alu_16bits_1_s, alu_16bits_2_s, alu_16bits_3_s, bit_extender_1_out, bit_extender_2_out,
       multiplexer_3_out, multiplexer_4_out, multiplexer_5_out, multiplexer_6_out, ram_1_dout,
       registers_8x16_1_r1, registers_8x16_1_r2;
  wire [15:7] memoriaDeInstrucoes_data_2;

  Clock Automatico (.out(Automatico_out));
  not not_1 (not_1_out, Clear_t);
  Multiplexer multiplexer_1 (.in0(Manual), .in1(Automatico_out), .out(CLK_t), .sel(controlled_buffer_1_out));
  assign controlled_buffer_1_out = not_1_out ? CLK : 1'bz;  // Controlled_Buffer controlled_buffer_1
  D_Flip_Flop d_ff_1 (.D(not_2_out), .clk(not_4_out), .Q(d_ff_1_q), .preset(in_15));  // open: Qn, reset
  not not_2 (not_2_out, Restart);
  not not_3 (not_3_out, Restart);
  not not_4 (not_4_out, not_3_out);
  assign bit_extender_1_out = {{11{program_cointer_1_saida[4]}}, program_cointer_1_saida};  // Bit_Extender bit_extender_1
  program_cointer program_cointer_1 (
    .Entrada(multiplexer_6_out[4:0]), .Clock(CLK_t), .Clear(Clear_t), .Saida(program_cointer_1_saida));
  ROM #(.addrWidth(5), .dataWidth(16)) memoriaDeInstrucoes (
    .addr(program_cointer_1_saida), .data({memoriaDeInstrucoes_data_2, memoriaDeInstrucoes_data}));
  ALU_16bits alu_16bits_1 (
    .SEL(3'b000), .A(16'h1), .B(bit_extender_1_out), .S(alu_16bits_1_s));  // open: Zero, Negative
  or or_1 (Clear_t, d_ff_1_q, Clear);
  // Probe on {memoriaDeInstrucoes_data_2, memoriaDeInstrucoes_data}
  // Probe on memoriaDeInstrucoes_data[2:0]
  // Probe on memoriaDeInstrucoes_data[5:3]
  // Probe on {memoriaDeInstrucoes_data_2[8:7], memoriaDeInstrucoes_data[6]}
  // Probe on memoriaDeInstrucoes_data_2[11:9]
  // Probe on memoriaDeInstrucoes_data_2[15:12]
  assign bit_extender_2_out = {{9{memoriaDeInstrucoes_data[6]}}, memoriaDeInstrucoes_data};  // Bit_Extender bit_extender_2
  // Probe on multiplexer_4_out
  Multiplexer #(.width(3)) multiplexer_2 (
    .in0(memoriaDeInstrucoes_data[5:3]),
    .in1({memoriaDeInstrucoes_data_2[8:7], memoriaDeInstrucoes_data[6]}), .out(multiplexer_2_out), .sel(in_8));
  Registers_8x16 registers_8x16_1 (
    .read1(memoriaDeInstrucoes_data_2[11:9]),
    .read2({memoriaDeInstrucoes_data_2[8:7], memoriaDeInstrucoes_data[6]}), .RegWrite(in_12),
    .Entrada(multiplexer_4_out), .write(multiplexer_2_out), .CLK(CLK_t), .r1(registers_8x16_1_r1),
    .r2(registers_8x16_1_r2));  // open: Reset
  ALU_16bits alu_16bits_2 (
    .SEL(3'b000), .A(alu_16bits_1_s), .B(bit_extender_2_out), .S(alu_16bits_2_s));  // open: Zero, Negative
  Multiplexer #(.width(16)) multiplexer_3 (
    .in0(registers_8x16_1_r2), .in1(bit_extender_2_out), .out(multiplexer_3_out), .sel(in_11));
  Multiplexer #(.width(16)) multiplexer_4 (.in0(alu_16bits_3_s), .in1(ram_1_dout), .out(multiplexer_4_out), .sel(in_6));
  ALU_16bits alu_16bits_3 (
    .SEL(memoriaDeInstrucoes_data[2:0]), .A(registers_8x16_1_r1), .B(multiplexer_3_out),
    .Zero(alu_16bits_3_zero), .S(alu_16bits_3_s));  // open: Negative
  Multiplexer #(.width(16)) multiplexer_5 (
    .in0(alu_16bits_1_s), .in1(alu_16bits_2_s), .out(multiplexer_5_out), .sel(and_1_out));
  and and_1 (and_1_out, in_13, alu_16bits_3_zero);
  Multiplexer #(.width(16)) multiplexer_6 (
    .in0(multiplexer_5_out), .in1(bit_extender_2_out), .out(multiplexer_6_out), .sel(in_14));
  RAM #(.addrWidth(5), .dataWidth(16)) ram_1 (
    .addr(alu_16bits_3_s[4:0]), .we(in_3), .oe(in_5), .clk(CLK_t), .din(registers_8x16_1_r2),
    .dout(ram_1_dout));

  // Other names for the same wires on the sheet: ALUOp0 = in_9; ALUOp1 = in_10; ALUSrc = in_11; Branch = in_13;
  //   Halt = in_15; Jump = in_14; MemRead = in_5; MemtoReg = in_6; MemWrite = in_3; RegDst = in_8; RegReset = Clear;
  //   RegWrite = in_12

  // Notes on the sheet:
  //   PC
  //   Ele tem o papel de apontar o endereço da memória a ser usada que contém uma instrução
  //   ULA
  //   É ondo é feito todas as operações lógicas e aritméticas das instruções, presente em quase todas as instruções.
  //   ROM
  //   Aqui é armazenado todas as instruções que o programa irá rodar, podendo ser previamente  
  //   carregado em um arquivo com as instruções com código de máquina.
  //   RAM
  //   Definitivo das operações a qual o usuário deseja guardar, sendo ele volátil, ou seja, 
  //   Banco de Registradores
  //   No banco de registradores temos um conjunto de registradores que serve 
  //   para auxiliar em operações e armazenar dados temporários dependendo de cada instrução
  //   caso o programa seja  encerrado de maneira indevida, os dados que estavam na memória se perderão.
  //   contents of memoriaDeInstrucoes (hex, n*v repeats v):
  //   5085
  //   MIP'S 
  //   Controle Manual 
  //   Instruct
  //   ADDI
  //   ADDI 
  //   ADD
  //   Sub
  //   SW
  //   LW
  //   $2<= $0 + 5
  //   $3<= $0 +3
  //   0101
  //   0000
  //   0000
  //   0011
  //   0010
  //   Minemônico
  //   $4<= $2 + $3
  //   $5<= $2- $3
  //   Mem($0 + 0) <= $2
  //   $0 <= Mem($3 - 3)
  //   opcode
  //   0101
  //   rs
  //   000
  //   000
  //   011
  //   011
  //   000
  //   011
  //   Hexadecimal
  //   5085
  //   50C3
  //   06A0
  //   04e9
  //   3080
  //   2603
  //   rt
  //   010
  //   011
  //   010
  //   010
  //   010
  //   000
  //   rd
  //   100
  //   101
  //   function
  //   000101
  //   000011
  //   000
  //   001
  //   000000
  //   000011
endmodule

module program_cointer (
  input  [4:0] Entrada,
  input  Clock,
  input  Clear,
  output [4:0] Saida
);

  D_Flip_Flop #(.trigger("falling")) d_ff_1 (
    .D(Entrada[4]), .clk(Clock), .Q(Saida[4]), .reset(Clear));  // open: Qn, preset
  D_Flip_Flop #(.trigger("falling")) d_ff_2 (
    .D(Entrada[3]), .clk(Clock), .Q(Saida[3]), .reset(Clear));  // open: Qn, preset
  D_Flip_Flop #(.trigger("falling")) d_ff_3 (
    .D(Entrada[2]), .clk(Clock), .Q(Saida[2]), .reset(Clear));  // open: Qn, preset
  D_Flip_Flop #(.trigger("falling")) d_ff_4 (
    .D(Entrada[1]), .clk(Clock), .Q(Saida[1]), .reset(Clear));  // open: Qn, preset
  D_Flip_Flop #(.trigger("falling")) d_ff_5 (
    .D(Entrada[0]), .clk(Clock), .Q(Saida[0]), .reset(Clear));  // open: Qn, preset
endmodule

module Registers_8x16 (
  input  [15:0] Entrada,
  input  RegWrite,
  input  [2:0] read1,
  input  [2:0] write,
  input  [2:0] read2,
  input  Reset,
  input  CLK,
  output [15:0] r1,
  output [15:0] r2
);

  wire [15:0] register_1_q, register_2_q, register_3_q, register_4_q, register_5_q, register_6_q,
       register_7_q, register_8_q;
  wire [16:0] demultiplexer_1_out0, demultiplexer_1_out1, demultiplexer_1_out2, demultiplexer_1_out3,
       demultiplexer_1_out4, demultiplexer_1_out5, demultiplexer_1_out6, demultiplexer_1_out7;

  Demultiplexer #(.select(3), .width(17)) demultiplexer_1 (
    .out0(demultiplexer_1_out0), .out1(demultiplexer_1_out1), .out2(demultiplexer_1_out2),
    .out3(demultiplexer_1_out3), .out4(demultiplexer_1_out4), .out5(demultiplexer_1_out5),
    .out6(demultiplexer_1_out6), .out7(demultiplexer_1_out7), .in({RegWrite, Entrada}), .sel(write));
  Register #(.width(16)) register_1 (
    .D(demultiplexer_1_out0[15:0]), .en(demultiplexer_1_out0[16]), .clk(CLK), .Q(register_1_q), .clr(Reset));
  Register #(.width(16)) register_2 (
    .D(demultiplexer_1_out1[15:0]), .en(demultiplexer_1_out1[16]), .clk(CLK), .Q(register_2_q), .clr(Reset));
  Register #(.width(16)) register_3 (
    .D(demultiplexer_1_out2[15:0]), .en(demultiplexer_1_out2[16]), .clk(CLK), .Q(register_3_q), .clr(Reset));
  Register #(.width(16)) register_4 (
    .D(demultiplexer_1_out3[15:0]), .en(demultiplexer_1_out3[16]), .clk(CLK), .Q(register_4_q), .clr(Reset));
  Register #(.width(16)) register_5 (
    .D(demultiplexer_1_out4[15:0]), .en(demultiplexer_1_out4[16]), .clk(CLK), .Q(register_5_q), .clr(Reset));
  Register #(.width(16)) register_6 (
    .D(demultiplexer_1_out5[15:0]), .en(demultiplexer_1_out5[16]), .clk(CLK), .Q(register_6_q), .clr(Reset));
  Register #(.width(16)) register_7 (
    .D(demultiplexer_1_out6[15:0]), .en(demultiplexer_1_out6[16]), .clk(CLK), .Q(register_7_q), .clr(Reset));
  Register #(.width(16)) register_8 (
    .D(demultiplexer_1_out7[15:0]), .en(demultiplexer_1_out7[16]), .clk(CLK), .Q(register_8_q), .clr(Reset));
  Multiplexer #(.select(3), .width(16)) multiplexer_1 (
    .in0(register_1_q), .in1(register_2_q), .in2(register_3_q), .in3(register_4_q), .in4(register_5_q),
    .in5(register_6_q), .in6(register_7_q), .in7(register_8_q), .out(r1), .sel(read1));
  Multiplexer #(.select(3), .width(16)) multiplexer_2 (
    .in0(register_1_q), .in1(register_2_q), .in2(register_3_q), .in3(register_4_q), .in4(register_5_q),
    .in5(register_6_q), .in6(register_7_q), .in7(register_8_q), .out(r2), .sel(read2));
endmodule

module somador_1bit (
  input  A,
  input  B,
  input  Cin,
  output Cout,
  output Soma
);

  wire and_1_out, and_2_out, and_3_out, and_4_out, and_5_out, xnor_1_out, xor_1_out;

  and and_1 (and_1_out, A, B);
  and and_2 (and_2_out, A, Cin);
  and and_3 (and_3_out, B, Cin);
  xnor xnor_1 (xnor_1_out, A, B);
  xor xor_1 (xor_1_out, A, B);
  or or_1 (Cout, and_1_out, and_2_out, and_3_out);
  and and_4 (and_4_out, xnor_1_out, Cin);
  and and_5 (and_5_out, xor_1_out, ~Cin);  // AND_Gate
  or or_2 (Soma, and_4_out, and_5_out);
endmodule

module somador_subtrator_1bit (
  input  Sub,
  input  Cin,
  input  A,
  input  B,
  output S,
  output Cout
);

  wire xor_1_out;

  xor xor_1 (xor_1_out, Sub, B);
  somador_1bit somador_1bit_1 (.A(A), .B(xor_1_out), .Cin(Cin), .Cout(Cout), .Soma(S));
endmodule

module ALU_1bit (
  input  A,
  input  B,
  input  Cin,
  input  [2:0] sel,
  output Cout,
  output S
);

  wire and_1_out, nand_1_out, nor_1_out, or_1_out, somador_subtrator_1bit_1_s, xor_1_out;

  somador_subtrator_1bit somador_subtrator_1bit_1 (
    .A(A), .B(B), .Sub(sel[0]), .Cin(Cin), .Cout(Cout), .S(somador_subtrator_1bit_1_s));
  and and_1 (and_1_out, B, A);
  or or_1 (or_1_out, A, B);
  nand nand_1 (nand_1_out, A, B);
  nor nor_1 (nor_1_out, A, B);
  xor xor_1 (xor_1_out, A, B);
  Multiplexer #(.select(3)) multiplexer_1 (
    .in0(somador_subtrator_1bit_1_s), .in1(somador_subtrator_1bit_1_s), .in2(and_1_out), .in3(or_1_out),
    .in4(nand_1_out), .in5(nor_1_out), .in6(xor_1_out), .out(S), .sel(sel));  // open: in7
endmodule

module ALU_16bits (
  input  [2:0] SEL,
  input  [15:0] A,
  input  [15:0] B,
  output [15:0] S,
  output Negative,
  output Zero
);

  wire alu_1bit_1_cout, alu_1bit_2_cout, alu_1bit_3_cout, alu_1bit_4_cout, alu_1bit_5_cout, alu_1bit_6_cout,
       alu_1bit_7_cout, alu_1bit_8_cout, alu_1bit_9_cout, alu_1bit_10_cout, alu_1bit_11_cout,
       alu_1bit_12_cout, alu_1bit_13_cout, alu_1bit_14_cout, alu_1bit_15_cout, and_1_out;
  wire [6:0] alu_1bit_9_s;
  wire [7:0] alu_1bit_1_s;

  ALU_1bit alu_1bit_1 (.sel(SEL), .A(A[0]), .B(B[0]), .Cin(SEL[0]), .Cout(alu_1bit_1_cout), .S(alu_1bit_1_s[0]));
  ALU_1bit alu_1bit_2 (
    .sel(SEL), .A(A[1]), .B(B[1]), .Cin(alu_1bit_1_cout), .Cout(alu_1bit_2_cout), .S(alu_1bit_1_s[1]));
  ALU_1bit alu_1bit_3 (
    .sel(SEL), .A(A[2]), .B(B[2]), .Cin(alu_1bit_2_cout), .Cout(alu_1bit_3_cout), .S(alu_1bit_1_s[2]));
  ALU_1bit alu_1bit_4 (
    .sel(SEL), .A(A[3]), .B(B[3]), .Cin(alu_1bit_3_cout), .Cout(alu_1bit_4_cout), .S(alu_1bit_1_s[3]));
  ALU_1bit alu_1bit_5 (
    .sel(SEL), .A(A[4]), .B(B[4]), .Cin(alu_1bit_4_cout), .Cout(alu_1bit_5_cout), .S(alu_1bit_1_s[4]));
  ALU_1bit alu_1bit_6 (
    .sel(SEL), .A(A[5]), .B(B[5]), .Cin(alu_1bit_5_cout), .Cout(alu_1bit_6_cout), .S(alu_1bit_1_s[5]));
  ALU_1bit alu_1bit_7 (
    .sel(SEL), .A(A[6]), .B(B[6]), .Cin(alu_1bit_6_cout), .Cout(alu_1bit_7_cout), .S(alu_1bit_1_s[6]));
  ALU_1bit alu_1bit_8 (
    .sel(SEL), .A(A[7]), .B(B[7]), .Cin(alu_1bit_7_cout), .Cout(alu_1bit_8_cout), .S(alu_1bit_1_s[7]));
  ALU_1bit alu_1bit_9 (
    .sel(SEL), .A(A[8]), .B(B[8]), .Cin(alu_1bit_8_cout), .Cout(alu_1bit_9_cout), .S(alu_1bit_9_s[0]));
  ALU_1bit alu_1bit_10 (
    .sel(SEL), .A(A[9]), .B(B[9]), .Cin(alu_1bit_9_cout), .Cout(alu_1bit_10_cout), .S(alu_1bit_9_s[1]));
  ALU_1bit alu_1bit_11 (
    .sel(SEL), .A(A[10]), .B(B[10]), .Cin(alu_1bit_10_cout), .Cout(alu_1bit_11_cout), .S(alu_1bit_9_s[2]));
  ALU_1bit alu_1bit_12 (
    .sel(SEL), .A(A[11]), .B(B[11]), .Cin(alu_1bit_11_cout), .Cout(alu_1bit_12_cout), .S(alu_1bit_9_s[3]));
  ALU_1bit alu_1bit_13 (
    .sel(SEL), .A(A[12]), .B(B[12]), .Cin(alu_1bit_12_cout), .Cout(alu_1bit_13_cout), .S(alu_1bit_9_s[4]));
  ALU_1bit alu_1bit_14 (
    .sel(SEL), .A(A[13]), .B(B[13]), .Cin(alu_1bit_13_cout), .Cout(alu_1bit_14_cout), .S(alu_1bit_9_s[5]));
  ALU_1bit alu_1bit_15 (
    .sel(SEL), .A(A[14]), .B(B[14]), .Cin(alu_1bit_14_cout), .Cout(alu_1bit_15_cout), .S(alu_1bit_9_s[6]));
  ALU_1bit alu_1bit_16 (.sel(SEL), .A(A[15]), .B(B[15]), .Cin(alu_1bit_15_cout), .S(Negative));  // open: Cout
  and and_1 (and_1_out, SEL[0], SEL[1], SEL[2]);
  Multiplexer #(.width(16)) multiplexer_1 (
    .in0({Negative, alu_1bit_9_s, alu_1bit_1_s}), .in1({{15{1'b0}}, Negative}), .out(S), .sel(and_1_out));
  nor nor_1 (Zero, alu_1bit_1_s[7], alu_1bit_1_s[0], alu_1bit_1_s[1], alu_1bit_1_s[2], alu_1bit_1_s[3], alu_1bit_1_s[4], alu_1bit_1_s[5], alu_1bit_1_s[6], alu_1bit_9_s[0], alu_1bit_9_s[1], alu_1bit_9_s[2], alu_1bit_9_s[3], alu_1bit_9_s[4], alu_1bit_9_s[5], alu_1bit_9_s[6], Negative);

  // Notes on the sheet:
  //   mnemonico
  //   ADD
  //   SUB
  //   AND
  //   OR
  //   OUT
  //   HLT
  //   código
  //   000
  //   001
  //   010
  //   100
  //   100
  //   111
  //   111
  //   endereço
  //   não tem
  //   XXXX
  //   XXXX
  //   XXXX
  //   XXXX
  //   não tem
  //   não tem
endmodule

module Controller (
  input  [2:0] OpCode,
  input  [15:0] Zero,
  output MemWrite,
  output MemRead,
  output MemtoReg,
  output RegDst,
  output ALUOp0,
  output ALUOp1,
  output ALUSrc,
  output RegWrite,
  output Branch,
  output Jump,
  output Hlt
);

  wire comparator_1_eq, demultiplexer_1_out0, demultiplexer_1_out1, demultiplexer_1_out7;

  Demultiplexer #(.select(3)) demultiplexer_1 (
    .out0(demultiplexer_1_out0), .out1(demultiplexer_1_out1), .out2(Jump), .out3(Hlt), .out4(MemRead),
    .out5(MemWrite), .out6(Branch), .out7(demultiplexer_1_out7), .in(1'b1), .sel(OpCode));
  Comparator #(.width(16)) comparator_1 (.a(Zero), .b({16{1'b0}}), .eq(comparator_1_eq));  // open: gt, lt
  or or_1 (RegDst, MemRead, demultiplexer_1_out1, demultiplexer_1_out7);
  or or_2 (ALUOp0, Branch, demultiplexer_1_out1);
  or or_3 (ALUOp1, demultiplexer_1_out0, demultiplexer_1_out1);
  or or_4 (ALUSrc, MemRead, MemWrite, demultiplexer_1_out7, demultiplexer_1_out1);
  or or_5 (RegWrite, demultiplexer_1_out0, MemRead, demultiplexer_1_out7, demultiplexer_1_out1);

  assign MemtoReg = MemRead;

  // Notes on the sheet:
  //   000
  //   Lw
  //   100
  //   101
  //   Sw
  //   111
  //   110
  //   Slti
  //   001
  //   010
  //   011
  //   Tipo R
  //   Addi
  //   Beq
  //   Jump
  //   Halt
endmodule

module ControleALU (
  input  [3:0] Funct,
  input  [1:0] OpALU,
  output [3:0] SelectALU
);

  wire and_1_out, and_2_out, and_3_out, and_4_out;

  and and_1 (and_1_out, ~OpALU[0], ~OpALU[1]);  // AND_Gate
  and and_2 (and_2_out, OpALU[0], ~OpALU[1]);  // AND_Gate
  and and_3 (and_3_out, ~OpALU[0], OpALU[1]);  // AND_Gate
  and and_4 (and_4_out, OpALU[0], OpALU[1]);
  assign SelectALU = and_3_out ? Funct : 4'bz;  // Controlled_Buffer controlled_buffer_1
  assign SelectALU = and_2_out ? 4'b0001 : 4'bz;  // Controlled_Buffer controlled_buffer_2
  assign SelectALU = and_1_out ? 4'b0000 : 4'bz;  // Controlled_Buffer controlled_buffer_3
  assign SelectALU = and_4_out ? 4'b0111 : 4'bz;  // Controlled_Buffer controlled_buffer_4
endmodule
